# Fritzing sketch leituraAnalógica (saved by Fritzing 0.9.3b)
breadboards: 1

parts:
  LED1 = LED - 5mm [color="Red (633nm)" package="5 mm [THT]"]
  R1 = Resistor [tolerance=±5% resistance=220 package=THT]
  Componente1 = Arduino Uno (Rev3)
  R2 = Photocell (LDR) [package=THT]
  R3 = Resistor [tolerance=±5% resistance=10k package=THT]

nets:
  N1: LED1.cathode, R1.Pin_0
  N2: LED1.anode, Componente1.D13/SCK
  N3: R1.Pin_1, Componente1.GND, R3.Pin_1
  N4: Componente1.A0, R2.pin_0, R3.Pin_0
  N5: Componente1.5V, R2.pin_1
