# Fritzing sketch automacao (saved by Fritzing 0.9.3b)
breadboards: 1

parts:
  LED1 = LED - 5mm [color="Red (633nm)" package="5 mm [THT]"]
  LED2 = LED - 5mm [color="Red (633nm)" package="5 mm [THT]"]
  R1 = Resistor [tolerance=±5% resistance=220 package=THT]
  R2 = Resistor [tolerance=±5% resistance=220 package=THT]
  Componente1 = Arduino Uno (Rev3)

nets:
  N1: LED1.cathode, R1.Pin_0
  N2: LED2.cathode, R2.Pin_0
  N3: R1.Pin_1, R2.Pin_1, Componente1.D12/MISO, Componente1.D13/SCK, Componente1.GND
