# Fritzing sketch automacaoII (saved by Fritzing 0.9.3b)
breadboards: 1

parts:
  LED1 = LED - 5mm [color="Red (633nm)" package="5 mm [THT]"]
  LED2 = LED - 5mm [color="Red (633nm)" package="5 mm [THT]"]
  R1 = Resistor [tolerance=±5% resistance=220 package=THT]
  R2 = Resistor [tolerance=±5% resistance=220 package=THT]
  Componente1 = Arduino Uno (Rev3)
  Componente2 = Bluetooth HC-05 Macho
  R3 = Resistor [tolerance=±5% resistance=1k package=THT]
  R4 = Resistor [tolerance=±5% resistance=2.2k package=THT]

nets:
  N1: LED1.cathode, R1.Pin_0
  N2: LED1.anode, Componente1.D13/SCK
  N3: LED2.cathode, R2.Pin_0
  N4: LED2.anode, Componente1.D12/MISO
  GND: R1.Pin_1, R2.Pin_1, Componente1.GND, Componente2.GND, R4.Pin_1
  N5: Componente1.D0/RX, Componente2.TXD
  N6: Componente1.D1/TX, R3.Pin_0
  5V: Componente1.5V, Componente2.VCC
  N7: Componente2.RXD, R3.Pin_1, R4.Pin_0
