# Fritzing sketch Atividade 2 (saved by Fritzing 0.9.3b)
breadboards: 1

parts:
  S1 = Pushbutton [package="[THT]"]
  S2 = Pushbutton [package="[THT]"]
  R1 = Resistor [tolerance=±5% resistance=10k package=THT]
  R2 = Resistor [tolerance=±5% resistance=10k package=THT]
  Componente1 = Arduino Uno (Rev3)
  J1 = Basic Servo

nets:
  N1: S1.Pin_1, S1.Pin_2, R1.Pin_0, Componente1.D3_PWM
  5V: S1.Pin_3, S1.Pin_4, S2.Pin_3, S2.Pin_4, Componente1.5V, J1.vcc
  N2: S2.Pin_1, S2.Pin_2, R2.Pin_0, Componente1.D2
  GND: R1.Pin_1, R2.Pin_1, Componente1.GND, J1.gnd
