# Fritzing sketch Untitled Sketch 2 (saved by Fritzing 0.9.3b)
breadboards: 1

parts:
  hc-sr1 = hc-sr04
  Componente1 = Arduino Uno (Rev3)
  LED1 = LED - 5mm [color="Red (633nm)" package="5 mm [THT]"]
  R1 = Resistor [tolerance=±5% resistance=220 package=THT]

nets:
  VCC: hc-sr1.VCC, Componente1.5V
  GND: hc-sr1.GND, Componente1.GND, R1.Pin_1
  N1: Componente1.D8, LED1.anode
  N2: LED1.cathode, R1.Pin_0
