# Fritzing sketch Controle de estacionamento (saved by Fritzing 0.9.3b)
breadboards: 1

parts:
  Componente1 = Arduino Uno (Rev3)
  Componente2 = Bluetooth HC-05 Macho
  R3 = Resistor [tolerance=±5% resistance=1k package=THT]
  R4 = Resistor [tolerance=±5% resistance=2.2k package=THT]
  hc-sr1 = hc-sr04
  LED1 = LED - 5mm [color="Red (633nm)" package="5 mm [THT]"]
  LED2 = LED - 5mm [color="Green (570nm)" package="5 mm [THT]"]
  R5 = Resistor [tolerance=±5% resistance=100 package=THT]
  R6 = Resistor [tolerance=±5% resistance=100 package=THT]

nets:
  N1: Componente1.D12/MISO, hc-sr1.Trig
  N2: Componente1.D13/SCK, hc-sr1.Echo
  N3: Componente1.D0/RX, Componente2.TXD
  N4: Componente1.D1/TX, R3.Pin_0
  N5: Componente1.D2, LED1.anode
  N6: Componente1.D3_PWM, LED2.anode
  VCC: Componente1.5V, Componente2.VCC, hc-sr1.VCC
  GND: Componente1.GND, Componente2.GND, R4.Pin_1, hc-sr1.GND, R5.Pin_1, R6.Pin_1
  N7: Componente2.RXD, R3.Pin_1, R4.Pin_0
  N8: LED1.cathode, R5.Pin_0
  N9: LED2.cathode, R6.Pin_0
