# Fritzing sketch robo (saved by Fritzing 0.9.3b)
breadboards: 2

parts:
  VCC1 = Battery block 9V
  S1 = Toggle Switch [package=THT]
  IC1 = L293D [package=THT]
  Componente1 = Arduino Uno (Rev3)
  M1 = DC Motor
  M2 = DC Motor
  hc-sr1 = hc-sr04

nets:
  GND: VCC1.-, IC1.0V, Componente1.GND, hc-sr1.GND
  N1: VCC1.+, S1.COM, S1.L2
  N2: S1.L1, IC1.+Vmotor, Componente1.VIN
  5V: IC1.Enable_1, IC1.Enable_2, IC1.+V, Componente1.5V, hc-sr1.VCC
  N3: IC1.In_1, Componente1.D9_PWM
  N4: IC1.Out_1_(_Controlled_by_Enable_1_), M1.pin_2
  N5: IC1.Out_2_(_Controlled_by_Enable_1_), M1.pin_1
  N6: IC1.In_2, Componente1.D10_PWM/SS
  N7: IC1.In_3, Componente1.D5_PWM
  N8: IC1.Out_3_(_Controlled_by_Enable_2_), M2.pin_2
  N9: IC1.Out_4_(_Controlled_by_Enable_2_), M2.pin_1
  N10: IC1.In_4, Componente1.D6_PWM
  N11: Componente1.D12/MISO, hc-sr1.Trig
  N12: Componente1.D13/SCK, hc-sr1.Echo
