# Fritzing sketch servo (saved by Fritzing 0.9.3b)
breadboards: 1

parts:
  Componente1 = Arduino Uno (Rev3)
  J1 = Basic Servo
  S1 = Pushbutton [package="[THT]"]
  S2 = Pushbutton [package="[THT]"]
  R1 = Resistor [tolerance=±5% resistance=10k package=THT]
  R2 = Resistor [tolerance=±5% resistance=10k package=THT]

nets:
  N1: Componente1.D9_PWM, J1.pulse
  N2: Componente1.D2, S2.Pin_3, S2.Pin_4, R1.Pin_0
  N3: Componente1.D3_PWM, S1.Pin_3, S1.Pin_4, R2.Pin_0
  5V: Componente1.5V, J1.vcc, S1.Pin_1, S1.Pin_2, S2.Pin_1, S2.Pin_2
  GND: Componente1.GND, J1.gnd, R1.Pin_1, R2.Pin_1
